// Logisim project RV32_IM.circ as structural Verilog: 2 circuits, main circuit main
module main (
);

  wire [31:0] ADDR, DATA, INST, W_EN;

  Clock clock_1 (.out(W_EN[0]));
  RAM #(.addrWidth(24), .dataWidth(32), .enables("line")) ram_1 (
    .addr(ADDR[23:0]), .we(W_EN[0]), .clk(W_EN[0]), .din(DATA), .dout(INST));
  CPU cpu_1 (.in_1(INST), .in_2(W_EN[0]), .out_3(ADDR), .out_4(DATA), .out_5(W_EN));
  // Pins of 1 and 32 bits meet at W_EN
endmodule

module CPU (
  input  [31:0] in_1,
  input  in_2,
  output [31:0] out_3,
  output [31:0] out_4,
  output [31:0] out_5
);


  // Other names for the same wires on the sheet: CLK = in_2; RAM_ADDR[31:0] = out_3; RAM_DATA[31:0] = out_4;
  //   RAM_INSTRUCTION[31:0] = in_1; RAM_WRITE_EN[31:0] = out_5

  // Notes on the sheet:
  //   outputs
  //   I/O
  //   inputs
endmodule
